// Logisim project sintese_circuito_1_DEC.circ as structural Verilog: 1 circuit, main circuit main
module main (
  input  A,
  input  B,
  input  C,
  output Y
);

  wire decoder_1_out1, decoder_1_out2, decoder_1_out3, decoder_1_out5, decoder_1_out6;

  Decoder #(.select(3), .enable("false")) decoder_1 (
    .out1(decoder_1_out1), .out2(decoder_1_out2), .out3(decoder_1_out3), .out5(decoder_1_out5),
    .out6(decoder_1_out6), .sel({C, B, A}));  // open: out0, out4, out7
  or or_1 (Y, decoder_1_out6, decoder_1_out5, decoder_1_out3, decoder_1_out2, decoder_1_out1);
endmodule
