// Logisim project circuito_redundancias_Y1_Y2.circ as structural Verilog: 1 circuit, main circuit main
module main (
  input  A,
  input  B,
  input  C,
  output Y1,
  output Y2
);

  wire and_1_out, and_2_out, and_3_out, and_4_out, and_5_out, and_6_out, not_1_out, not_2_out, not_3_out;

  not not_1 (not_1_out, A);
  not not_2 (not_2_out, B);
  not not_3 (not_3_out, C);
  and and_1 (and_1_out, C, not_1_out);
  and and_2 (and_2_out, not_3_out, B);
  and and_3 (and_3_out, not_2_out, A);
  and and_4 (and_4_out, not_3_out, A);
  and and_5 (and_5_out, C, not_2_out);
  and and_6 (and_6_out, B, not_1_out);
  or or_1 (Y1, and_1_out, and_2_out, and_3_out);
  or or_2 (Y2, and_4_out, and_5_out, and_6_out);
endmodule
