// Logisim project projeto_no_7.circ as structural Verilog: 1 circuit, main circuit main
// a
module main (
  input  D,
  input  C,
  input  B,
  input  A
);

  wire a_out, a_t, b_out, b_t, c_out, c_t, d_out, e_out, f_out, g_out, not_1_out, not_2_out, not_3_out,
       not_4_out, PD_out, U1_A_out, U1_B_out, U1_C_out, U1_D_out, U2_A_out, U2_B_out;

  not not_1 (not_1_out, D);
  not not_2 (not_2_out, C);
  not not_3 (not_3_out, B);
  not not_4 (not_4_out, A);
  and U1_A (U1_A_out, A, not_3_out);
  and U1_B (U1_B_out, not_3_out, C);
  and U2_A (U2_A_out, not_4_out, not_3_out, not_1_out);
  and U2_B (U2_B_out, not_3_out, not_2_out, not_1_out);
  and U1_C (U1_C_out, B, C);
  and U1_D (U1_D_out, A, not_1_out);
  Button f (.out(f_out));
  Button g (.out(g_out));
  _7_Segment_Display u_7_segment_display_1 (
    .g(g_out), .f(f_out), .a(a_out), .b(b_out), .e(e_out), .d(d_out), .c(c_out), .dp(PD_out));
  Button e (.out(e_out));
  Button u_d (.out(d_out));
  or U3_A (a_t, U1_A_out, U1_B_out, D);
  _7_Segment_Display u_7_segment_display_2 (.a(a_t), .b(b_t), .c(c_t));  // open: g, f, e, d, dp
  Button u_a (.out(a_out));
  Button u_b (.out(b_out));
  Button PD (.out(PD_out));
  Button u_c (.out(c_out));
  or U3_B (b_t, U2_A_out, U2_B_out, U1_C_out);
  or U3_C (c_t, U1_C_out, U2_B_out, U1_D_out);

  // Notes on the sheet:
  //   U4:A~D
endmodule
