// Logisim project projeto_2024_1.circ as structural Verilog: 1 circuit, main circuit main
module main (
  input  m,
  input  q2,
  input  q1,
  input  q0,
  output d2,
  output d1,
  output d0
);

  wire and_1_out, and_2_out, and_3_out, and_4_out, and_5_out, and_6_out, and_7_out, and_8_out, and_9_out,
       not_1_out, not_2_out, not_3_out, not_4_out, not_5_out, not_6_out, not_7_out, not_8_out, not_9_out,
       not_10_out, not_11_out, not_12_out;

  not not_1 (not_1_out, m);
  and and_1 (and_1_out, not_1_out, not_2_out);
  not not_2 (not_2_out, q1);
  not not_3 (not_3_out, q2);
  and and_2 (and_2_out, q1, not_4_out);
  not not_4 (not_4_out, q0);
  and and_3 (and_3_out, m, q0);
  not not_5 (not_5_out, m);
  not not_6 (not_6_out, q1);
  and and_4 (and_4_out, not_5_out, not_6_out, q0);
  not not_7 (not_7_out, m);
  and and_5 (and_5_out, not_7_out, q2, q1);
  and and_6 (and_6_out, m, not_8_out, not_9_out);
  not not_8 (not_8_out, q1);
  not not_9 (not_9_out, q0);
  and and_7 (and_7_out, m, q1, q0);
  not not_10 (not_10_out, q0);
  not not_11 (not_11_out, m);
  and and_8 (and_8_out, not_11_out, q2, q1);
  and and_9 (and_9_out, m, not_12_out);
  not not_12 (not_12_out, q2);
  or or_1 (d2, and_1_out, not_3_out, and_2_out, and_3_out);
  or or_2 (d1, and_4_out, and_5_out, and_6_out, and_7_out);
  or or_3 (d0, not_10_out, and_8_out, and_9_out);
endmodule
