# Fritzing sketch gerador_senoidal_DAC (saved by Fritzing 0.9.5d)
breadboards: 1

parts:
  IRF640 = Basic FET N-Channel [package="TO220 [THT]"]
  C1 = Ceramic Capacitor [capacitance=3.3nF package="200 mil [THT, multilayer]"]
  R1 = Resistor [tolerance=±5% resistance=10k package="2512 [SMD]"]
  SP1 = SPEAKER [part_number="8 Ohms, 250 mW" package=pcb_mount_speaker]
  Arduino_Uno = Arduino Uno (Rev3) - ICSP
  DAC = MCP4725 [package=SOT23-6]

nets:
  N1: IRF640.gate, C1.1, R1.Pin_1
  N2: IRF640.drain, SP1.-
  GND: IRF640.source, C1.0, DAC.VSS
  N3: R1.Pin_0, DAC.VOUT
  5V: SP1.+, DAC.VDD
  N4: Arduino_Uno.A5/SCL, DAC.SCL
  N5: Arduino_Uno.A4/SDA, DAC.SDA

notes:
  Fonte externa!
  do Arduíno
