# Fritzing sketch ligacao_speaker_IRF640 (saved by Fritzing 0.9.5d)
breadboards: 1

parts:
  SP1 = SPEAKER [package=pcb_mount_speaker]
  Q1 = Basic FET N-Channel [package="TO220 [THT]"]

nets:
  N1: SP1.+, Q1.drain

notes:
  5V (externo)
  IRF 640
  saida analógica
  GND
